// Digital circuit P1 Julia e Leonardo - Desafio.dig as structural Verilog
module P1_Julia_e_Leonardo___Desafio (
  input  Envia,
  input  Clock,
  input  Limpa,
  input  [6:0] Entrada,
  input  Par,
  input  Impar,
  output T_X
);

  wire _7404_1_p6, _7404_1_p9, _7404_1_p10, _7408_1_p11, _7408_1_p12, _7408_1_p13, _7408_1_p14, _7408_2_p3,
       _7408_2_p7, _7408_2_p11, _7408_2_p12, _7408_3_p11, _7408_3_p12, _7432_3_p7, _7474_1_p2, _7474_1_p3,
       _7474_1_p11, _7474_1_p12, _7474_2_p2, _7474_2_p3, _7474_2_p6, _7474_2_p11, _7474_2_p12, _7474_3_p6,
       _74280_1_p12, _74280_1_p13;

  LED Pera (.in(_7474_1_p12));
  // _7474 _7474_1: pin names not known; wires that end beside it: 1'b1, _7474_1_p2, _7474_1_p3, Limpa, 1'b1, _7474_1_p3, _7474_1_p3, Limpa, 1'b1, 1'b0, _7474_1_p11, _7474_1_p12
  // _7404 _7404_1: pin names not known; wires that end beside it: 1'b0, 1'b0, 1'b0, 1'b0, Envia, _7404_1_p6, 1'b1, 1'b0, _7404_1_p9, _7404_1_p10
  // _7474 _7474_2: pin names not known; wires that end beside it: 1'b1, _7474_2_p2, _7474_2_p3, Limpa, 1'b1, _7474_2_p6, _7474_2_p3, Limpa, 1'b1, 1'b0, _7474_2_p11, _7474_2_p12
  LED D5 (.in(_7474_2_p12));
  LED D6 (.in(_7474_2_p11));
  // _7408 _7408_1: pin names not known; wires that end beside it: 1'b0, _7404_1_p10, _7404_1_p6, _7474_2_p11, _7404_1_p10, Entrada[6], _7474_2_p12, _7404_1_p6, 1'b1, 1'b0, _7408_1_p11, _7408_1_p12, _7408_1_p13, _7408_1_p14
  // _7408 _7408_2: pin names not known; wires that end beside it: Entrada[5], _7404_1_p10, _7408_2_p3, _7404_1_p6, _7404_1_p6, Clock, _7408_2_p7, _7404_1_p9, 1'b1, 1'b0, _7408_2_p11, _7408_2_p12, _7408_2_p7, _7474_1_p3
  // _7474 _7474_3: pin names not known; wires that end beside it: 1'b1, Envia, Envia, Limpa, 1'b1, _7474_3_p6, _7474_2_p3, Limpa, 1'b1, 1'b0, _7404_1_p6, _7474_1_p2
  LED Start (.in(_7474_1_p2));
  // _7432 _7432_1: pin names not known; wires that end beside it: _7408_1_p11, _7408_1_p12, _7408_1_p13, _7408_1_p14, _7408_2_p11, _7408_2_p12, Envia, _7474_1_p3, 1'b1, 1'b0, _7474_3_p6, _7474_2_p2, _7474_2_p6, _7474_2_p3
  // _74280 _74280_1: pin names not known; wires that end beside it: Entrada[0], Entrada[1], Entrada[2], Entrada[3], Entrada[4], Entrada[5], Entrada[6], 1'b0, 1'b0, 1'b1, 1'b0, _74280_1_p12, _74280_1_p13
  // _7432 _7432_2: pin names not known; wires that end beside it: _7474_1_p11, _7474_1_p12, 1'b0, 1'b0, 1'b0, 1'b0, 1'b0, 1'b0, 1'b1, 1'b0, T_X
  // _7408 _7408_3: pin names not known; wires that end beside it: _74280_1_p12, Par, Impar, _74280_1_p13, 1'b0, 1'b0, 1'b0, 1'b0, 1'b1, 1'b0, _7408_3_p11, _7408_3_p12, 1'b0
  // _7432 _7432_3: pin names not known; wires that end beside it: _7408_3_p11, _7408_3_p12, 1'b0, 1'b0, 1'b1, 1'b0, _7432_3_p7
  // _74166 _74166_1: pin names not known; wires that end beside it: _7404_1_p6, 1'b1, Envia, _7474_1_p3, 1'b1, 1'b1, _7432_3_p7, Entrada[0], Entrada[1], Entrada[2], Entrada[3], Entrada[4], 1'b1, 1'b0, Limpa, _7408_2_p3
  LED Paridade (.in(_7432_3_p7));
  LED D4 (.in(_7408_2_p3));

  // Notes on the sheet:
  //   Limpa: default 1
  //   Start
  //   A1
endmodule
