// Digital circuit exp7.dig as structural Verilog
module exp7 (
  input  Quantidade0,
  input  Reset,
  input  Pause,
  input  Pulso,
  input  Quantidade1,
  input  Quantidade2,
  input  Quantidade3,
  input  Producao0,
  input  Producao1,
  input  Producao2,
  input  Producao3,
  input  Carga,
  output Avanco,
  output Fim,
  output Inicia,
  output Interrompe,
  output CP0,
  output CP1,
  output CP2,
  output CP3,
  output CQ0,
  output CQ1,
  output CQ2,
  output CQ3
);

  wire _7474_1_pin2, _7474_1_pin5, _7474_1_pin8, _7474_2_pin5, _7474_2_pin9, _7474_3_pin5, _7474_3_pin9,
       _7474_4_pin5, _7474_4_pin9, _7474_5_pin5, _7474_5_pin9, _74163_1_pin9, and_1_out, and_3_out,
       and_4_out, and_5_out, not_1_out, or_1_out, xnor_1_out, xnor_2_out, xnor_3_out, xnor_4_out, xnor_5_out,
       xnor_6_out, xnor_7_out, xnor_8_out, xor_1_out;

  xor xor_1 (xor_1_out, Fim, Reset);
  _7474 _7474_1 (
    .pin1(1'b1), .pin2(_7474_1_pin2), .pin3(xor_1_out), .pin4(1'b1), .pin5(_7474_1_pin5),
    .pin6(_7474_1_pin2), .pin7(1'b0), .pin8(_7474_1_pin8), .pin9(Interrompe), .pin10(1'b1), .pin11(Pause),
    .pin12(_7474_1_pin8), .pin13(1'b1), .pin14(1'b1));
  and and_1 (and_1_out, Pulso, ~Interrompe);  // And
  _7474 _7474_2 (
    .pin1(1'b1), .pin2(Quantidade1), .pin3(Carga), .pin4(1'b1), .pin5(_7474_2_pin5), .pin7(1'b0),
    .pin9(_7474_2_pin9), .pin10(1'b1), .pin11(Carga), .pin12(Quantidade0), .pin13(1'b1), .pin14(1'b1));  // open: pin6, pin8
  _7474 _7474_3 (
    .pin1(1'b1), .pin2(Quantidade3), .pin3(Carga), .pin4(1'b1), .pin5(_7474_3_pin5), .pin7(1'b0),
    .pin9(_7474_3_pin9), .pin10(1'b1), .pin11(Carga), .pin12(Quantidade2), .pin13(1'b1), .pin14(1'b1));  // open: pin6, pin8
  _7474 _7474_4 (
    .pin1(1'b1), .pin2(Producao1), .pin3(Carga), .pin4(1'b1), .pin5(_7474_4_pin5), .pin7(1'b0),
    .pin9(_7474_4_pin9), .pin10(1'b1), .pin11(Carga), .pin12(Producao0), .pin13(1'b1), .pin14(1'b1));  // open: pin6, pin8
  _7474 _7474_5 (
    .pin1(1'b1), .pin2(Producao3), .pin3(Carga), .pin4(1'b1), .pin5(_7474_5_pin5), .pin7(1'b0),
    .pin9(_7474_5_pin9), .pin10(1'b1), .pin11(Carga), .pin12(Producao2), .pin13(1'b1), .pin14(1'b1));  // open: pin6, pin8
  not not_1 (not_1_out, Reset);
  and and_2 (Inicia, _7474_1_pin5, not_1_out);
  and and_3 (and_3_out, and_1_out, not_1_out);
  and and_4 (and_4_out, ~Inicia, and_3_out);  // And
  or or_1 (or_1_out, Avanco, and_4_out);
  _74163 _74163_1 (
    .pin1(Inicia), .pin2(and_3_out), .pin3(1'b1), .pin4(1'b0), .pin5(1'b0), .pin6(1'b0), .pin7(1'b1),
    .pin8(1'b0), .pin9(_74163_1_pin9), .pin10(1'b1), .pin11(CQ3), .pin12(CQ2), .pin13(CQ1), .pin14(CQ0),
    .pin16(1'b1));  // open: pin15
  _74163 _74163_2 (
    .pin1(Inicia), .pin2(or_1_out), .pin3(1'b0), .pin4(1'b0), .pin5(1'b0), .pin6(1'b0), .pin7(1'b1),
    .pin8(1'b0), .pin9(1'b1), .pin10(1'b1), .pin11(CP3), .pin12(CP2), .pin13(CP1), .pin14(CP0), .pin16(1'b1));  // open: pin15
  not not_2 (_74163_1_pin9, Avanco);
  // Probe on CP0
  // Probe on CP1
  // Probe on CP2
  // Probe on CP3
  and and_5 (and_5_out, ~CQ0, ~CQ1, ~CQ2, ~CQ3);  // And
  xnor xnor_1 (xnor_1_out, CQ0, _7474_2_pin9);
  xnor xnor_2 (xnor_2_out, CQ1, _7474_2_pin5);
  xnor xnor_3 (xnor_3_out, CQ2, _7474_3_pin9);
  xnor xnor_4 (xnor_4_out, CQ3, _7474_3_pin5);
  xnor xnor_5 (xnor_5_out, CP0, _7474_4_pin9);
  xnor xnor_6 (xnor_6_out, CP1, _7474_4_pin5);
  xnor xnor_7 (xnor_7_out, CP2, _7474_5_pin9);
  xnor xnor_8 (xnor_8_out, CP3, _7474_5_pin5);
  and and_6 (Avanco, xnor_1_out, xnor_2_out, ~and_5_out, xnor_3_out, xnor_4_out);  // And
  and and_7 (Fim, xnor_5_out, xnor_6_out, Avanco, xnor_7_out, xnor_8_out);

  // Notes on the sheet:
  //   Quantidade1: default 1
  //   Producao1: default 1
  //   Reg. Quantidade
  //   Reg. Produção
  //   Contador Quantidade
  //   Contador Produção
endmodule
