// Digital circuit fd_P2.dig as structural Verilog
module fd_P2 (
  input  [3:0] controle,
  input  clock,
  input  resetar,
  input  contar,
  input  alterar,
  output cheio,
  output vazio,
  output luz,
  output ar,
  output [3:0] contador,
  output up_down
);

  wire _7474_1_pin2, _7474_1_pin5, _74191_1_pin4, and_1_out, or_1_out;

  or or_1 (or_1_out, controle[0], controle[1], controle[2], controle[3]);
  and and_1 (and_1_out, or_1_out, clock);
  _7474 _7474_1 (
    .pin1(resetar), .pin2(_7474_1_pin2), .pin3(alterar), .pin4(1'b1), .pin5(_7474_1_pin5),
    .pin6(_7474_1_pin2), .pin7(1'b0), .pin10(1'b1), .pin11(1'b1), .pin12(1'b1), .pin13(1'b1), .pin14(1'b1));  // open: pin8, pin9
  _7474 _7474_2 (
    .pin1(resetar), .pin2(controle[1]), .pin3(and_1_out), .pin4(1'b1), .pin5(vazio), .pin7(1'b0),
    .pin9(cheio), .pin10(1'b1), .pin11(and_1_out), .pin12(controle[0]), .pin13(resetar), .pin14(1'b1));  // open: pin6, pin8
  _7474 _7474_3 (
    .pin1(resetar), .pin2(controle[3]), .pin3(and_1_out), .pin4(1'b1), .pin5(ar), .pin7(1'b0), .pin9(luz),
    .pin10(1'b1), .pin11(and_1_out), .pin12(controle[2]), .pin13(resetar), .pin14(1'b1));  // open: pin6, pin8
  _74191 _74191_1 (
    .pin1(1'b0), .pin2(contador[1]), .pin3(contador[0]), .pin4(_74191_1_pin4), .pin5(_7474_1_pin5),
    .pin6(contador[2]), .pin7(contador[3]), .pin8(1'b0), .pin9(1'b0), .pin10(1'b0), .pin11(resetar),
    .pin12(_74191_1_pin4), .pin14(contar), .pin15(1'b0), .pin16(1'b1));  // open: pin13
  not not_1 (up_down, _7474_1_pin5);

  // Notes on the sheet:
  //   resetar: default 1
  //   FLUXO DE DADOS
endmodule
