// Digital circuit registrador contador.dig as structural Verilog
module registrador_contador (
  input  D6,
  input  D5,
  input  D4,
  input  D3,
  input  D2,
  input  D1,
  input  D0,
  input  Limpa,
  input  Clock,
  input  Envia,
  input  SER,
  input  C,
  input  D,
  input  E,
  input  F,
  input  G,
  input  H,
  input  VCC,
  input  GND,
  input  nCLR,
  input  ENVIA_2,
  input  B,
  input  PAR,
  input  Clock_2,
  output xx,
  output Tx,
  output QH,
  output _0000,
  output Tx_2
);

  wire and_1_out, and_2_out, and_3_out, and_4_out, and_5_out, and_6_out, and_7_out, and_8_out, and_9_out,
       and_10_out, and_11_out, and_12_out, and_13_out, and_14_out, and_15_out, and_16_out, and_17_out,
       and_18_out, and_19_out, and_20_out, and_21_out, and_22_out, and_23_out, and_24_out, and_25_out,
       and_26_out, and_27_out, and_29_out, and_30_out, and_32_out, and_33_out, d_ff_as_1_q, d_ff_as_2_q,
       d_ff_as_3_q, d_ff_as_4_q, d_ff_as_5_q, d_ff_as_6_q, d_ff_as_7_q, d_ff_as_8_q, d_ff_as_9_q,
       d_ff_as_10_q, d_ff_as_11_q, d_ff_as_12_q, d_ff_as_13_q, d_ff_as_14_q, d_ff_as_15_q, d_ff_as_16_q,
       d_ff_as_17_q, d_ff_as_18_q, d_ff_as_19_q, not_1_out, not_2_out, not_3_out, not_4_out, not_5_out,
       not_6_out, not_7_out, not_8_out, not_9_out, not_10_out, not_11_out, or_1_out, or_2_out, or_3_out,
       or_4_out, or_5_out, or_6_out, or_7_out, or_8_out, or_9_out, or_10_out, or_11_out, or_13_out,
       or_14_out, or_15_out, xor_1_out, xor_2_out, xor_3_out, xor_4_out, xor_5_out, xor_6_out;
  wire [3:0] counter_1_out, counter_2_out;

  not not_1 (not_1_out, nCLR);
  and and_1 (and_1_out, SER, d_ff_as_2_q);
  PowerSupply powersupply_1 (.VDD(VCC), .GND(GND));
  or or_1 (or_1_out, and_1_out, and_2_out);
  and and_2 (and_2_out, not_2_out, PAR);
  not not_2 (not_2_out, d_ff_as_2_q);
  D_FF_AS d_ff_as_1 (.Set(1'b0), .D(or_1_out), .C(or_9_out), .Clr(not_1_out), .Q(d_ff_as_1_q));  // open: nQ
  and and_3 (and_3_out, xor_6_out, Envia);
  // Probe on d_ff_as_1_q
  and and_4 (and_4_out, d_ff_as_1_q, d_ff_as_2_q);
  D_FF_AS d_ff_as_2 (.Set(1'b0), .D(ENVIA_2), .C(ENVIA_2), .Clr(1'b0), .Q(d_ff_as_2_q));  // open: nQ
  // Probe on xor_6_out
  D_FF_AS d_ff_as_3 (.Set(and_3_out), .D(d_ff_as_18_q), .C(Clock), .Clr(Limpa), .Q(d_ff_as_3_q));  // open: nQ
  or or_2 (or_2_out, and_4_out, and_5_out);
  and and_5 (and_5_out, not_2_out, B);
  and and_6 (and_6_out, D6, Envia);
  // Probe on d_ff_as_3_q
  D_FF_AS d_ff_as_4 (.Set(and_6_out), .D(d_ff_as_3_q), .C(Clock), .Clr(Limpa), .Q(d_ff_as_4_q));  // open: nQ
  D_FF_AS d_ff_as_5 (.Set(1'b0), .D(or_2_out), .C(or_9_out), .Clr(not_1_out), .Q(d_ff_as_5_q));  // open: nQ
  and and_7 (and_7_out, D5, Envia);
  // Probe on d_ff_as_4_q
  // Probe on d_ff_as_5_q
  or or_3 (or_3_out, and_8_out, and_10_out);
  and and_8 (and_8_out, d_ff_as_5_q, d_ff_as_2_q);
  and and_9 (and_9_out, D4, Envia);
  D_FF_AS d_ff_as_6 (.Set(and_7_out), .D(d_ff_as_4_q), .C(Clock), .Clr(Limpa), .Q(d_ff_as_6_q));  // open: nQ
  D_FF_AS d_ff_as_7 (.Set(1'b0), .D(or_3_out), .C(or_9_out), .Clr(not_1_out), .Q(d_ff_as_7_q));  // open: nQ
  and and_10 (and_10_out, not_2_out, C);
  and and_11 (and_11_out, D3, Envia);
  // Probe on d_ff_as_6_q
  D_FF_AS d_ff_as_8 (.Set(and_9_out), .D(d_ff_as_6_q), .C(Clock), .Clr(Limpa), .Q(d_ff_as_8_q));  // open: nQ
  and and_12 (and_12_out, D2, Envia);
  // Probe on d_ff_as_8_q
  D_FF_AS d_ff_as_9 (.Set(and_11_out), .D(d_ff_as_8_q), .C(Clock), .Clr(Limpa), .Q(d_ff_as_9_q));  // open: nQ
  // Probe on d_ff_as_7_q
  or or_4 (or_4_out, and_13_out, and_15_out);
  and and_13 (and_13_out, d_ff_as_7_q, d_ff_as_2_q);
  and and_14 (and_14_out, D1, Envia);
  // Probe on d_ff_as_9_q
  D_FF_AS d_ff_as_10 (.Set(and_12_out), .D(d_ff_as_9_q), .C(Clock), .Clr(Limpa), .Q(d_ff_as_10_q));  // open: nQ
  D_FF_AS d_ff_as_11 (.Set(1'b0), .D(or_4_out), .C(or_9_out), .Clr(not_1_out), .Q(d_ff_as_11_q));  // open: nQ
  and and_15 (and_15_out, not_2_out, D);
  and and_16 (and_16_out, D0, Envia);
  // Probe on d_ff_as_10_q
  // Probe on d_ff_as_11_q
  and and_17 (and_17_out, d_ff_as_11_q, d_ff_as_2_q);
  xor xor_1 (xor_1_out, D6, D5);
  xor xor_2 (xor_2_out, D4, D3);
  xor xor_3 (xor_3_out, D2, D1);
  D_FF_AS d_ff_as_12 (.Set(and_14_out), .D(d_ff_as_10_q), .C(Clock), .Clr(Limpa), .Q(d_ff_as_12_q));  // open: nQ
  or or_5 (or_5_out, and_17_out, and_18_out);
  and and_18 (and_18_out, not_2_out, E);
  not not_3 (not_3_out, or_15_out);
  xor xor_4 (xor_4_out, xor_1_out, xor_2_out);
  xor xor_5 (xor_5_out, D0, xor_3_out);
  // Probe on d_ff_as_12_q
  D_FF_AS d_ff_as_13 (.Set(and_16_out), .D(d_ff_as_12_q), .C(Clock), .Clr(Limpa), .Q(d_ff_as_13_q));  // open: nQ
  D_FF_AS d_ff_as_14 (.Set(1'b0), .D(or_5_out), .C(or_9_out), .Clr(not_1_out), .Q(d_ff_as_14_q));  // open: nQ
  and and_19 (and_19_out, Clock_2, not_3_out);
  and and_20 (and_20_out, 1'b1, Envia);
  // Probe on d_ff_as_13_q
  D_FF_AS d_ff_as_15 (.Set(1'b0), .D(d_ff_as_13_q), .C(Clock), .Clr(Limpa), .Q(d_ff_as_15_q));  // open: nQ
  // Probe on d_ff_as_14_q
  and and_21 (and_21_out, d_ff_as_14_q, d_ff_as_2_q);
  xor xor_6 (xor_6_out, xor_4_out, xor_5_out);
  or or_6 (or_6_out, and_21_out, and_22_out);
  and and_22 (and_22_out, not_2_out, F);
  // Probe on d_ff_as_15_q
  D_FF_AS d_ff_as_16 (.Set(and_20_out), .D(d_ff_as_15_q), .C(Clock), .Clr(Limpa), .Q(d_ff_as_16_q));  // open: nQ
  D_FF_AS d_ff_as_17 (.Set(1'b0), .D(or_6_out), .C(or_9_out), .Clr(not_1_out), .Q(d_ff_as_17_q));  // open: nQ
  // Probe on d_ff_as_16_q
  // Probe on d_ff_as_17_q
  or or_7 (or_7_out, and_23_out, and_24_out);
  and and_23 (and_23_out, d_ff_as_17_q, d_ff_as_2_q);
  D_FF_AS d_ff_as_18 (.Set(and_20_out), .D(d_ff_as_16_q), .C(Clock), .Clr(Limpa), .Q(d_ff_as_18_q));  // open: nQ
  D_FF_AS d_ff_as_19 (.Set(1'b0), .D(or_7_out), .C(or_9_out), .Clr(not_1_out), .Q(d_ff_as_19_q));  // open: nQ
  and and_24 (and_24_out, not_2_out, G);
  // Probe on d_ff_as_18_q
  Counter #(.Bits(4)) counter_1 (.en(1'b1), .C(Clock), .clr(and_29_out), .out(counter_1_out));  // open: ovf
  // Probe on d_ff_as_19_q
  or or_8 (or_8_out, and_25_out, and_26_out);
  and and_25 (and_25_out, d_ff_as_19_q, d_ff_as_2_q);
  D_FF_AS d_ff_as_20 (.Set(1'b0), .D(or_8_out), .C(or_9_out), .Clr(not_1_out), .Q(QH));  // open: nQ
  and and_26 (and_26_out, not_2_out, H);
  not not_4 (not_4_out, counter_1_out[0]);
  or or_9 (or_9_out, ENVIA_2, and_19_out);
  not not_5 (not_5_out, counter_1_out[1]);
  not not_6 (not_6_out, counter_1_out[2]);
  Counter #(.Bits(4)) counter_2 (.en(1'b1), .C(Clock_2), .clr(and_32_out), .out(counter_2_out));  // open: ovf
  not not_7 (not_7_out, counter_1_out[3]);
  and and_27 (and_27_out, counter_1_out[0], not_5_out, not_6_out, counter_1_out[3]);
  and and_28 (xx, not_7_out, not_6_out, not_5_out, not_4_out);
  and and_29 (and_29_out, not_4_out, counter_1_out[1], not_6_out, counter_1_out[3]);
  not not_8 (not_8_out, counter_2_out[0]);
  not not_9 (not_9_out, counter_2_out[1]);
  or or_10 (or_10_out, and_27_out, or_11_out);
  or or_11 (or_11_out, xx, and_29_out);
  not not_10 (not_10_out, counter_2_out[2]);
  not not_11 (not_11_out, counter_2_out[3]);
  or or_12 (Tx, d_ff_as_16_q, or_10_out);
  and and_30 (and_30_out, counter_2_out[0], not_9_out, not_10_out, counter_2_out[3]);
  and and_31 (_0000, not_11_out, not_10_out, not_9_out, not_8_out);
  and and_32 (and_32_out, not_8_out, counter_2_out[1], not_10_out, counter_2_out[3]);
  and and_33 (and_33_out, counter_2_out[0], not_9_out, not_10_out, not_11_out);
  or or_13 (or_13_out, and_30_out, or_14_out);
  or or_14 (or_14_out, _0000, and_32_out);
  or or_15 (or_15_out, _0000, and_33_out);
  or or_16 (Tx_2, QH, or_13_out);

  // Notes on the sheet:
  //   D5: default 1
  //   D4: default 1
  //   SER: pin 1
  //   C: pin 4, default 1
  //   D: pin 5, default 1
  //   E: pin 10
  //   F: pin 11
  //   G: pin 12
  //   H: pin 14
  //   QH: pin 13
  //   VCC: pin 16, default 1
  //   GND: pin 8
  //   nCLR: pin 9, default 1
  //   B: pin 4
endmodule
